// Logisim project ALU.circ as structural Verilog: 1 circuit, main circuit ALU
module ALU (
  input  [31:0] A,
  input  [31:0] B,
  input  [4:0] Shift,
  input  [3:0] Codop,
  input  CarryIn,
  output [31:0] S,
  output [3:0] Flags
);

  wire ADC_Cout, and_3_out, and_4_out, bitselector_1_out, bitselector_2_out, bitselector_3_out,
       bitselector_4_out, bitselector_5_out, CMN_Cout, CMP_Cout, not_1_out, SBC_Cout, xor_2_out, xor_3_out;
  wire [4:0] negator_2_out, subtractor_3_out;
  wire [31:0] adder_1_out, and_2_out, CMN, CMP, multiplier_1_out, negator_1_out, not_2_out, or_1_out, s_t,
       shifter_1_out, shifter_2_out, shifter_3_out, shifter_4_out, subtractor_1_out, TST, xor_1_out;

  assign TST = A & B;  // AND_Gate and_1, 32 bits wide
  assign xor_1_out = A ^ B;  // XOR_Gate xor_1, 32 bits wide
  Shifter #(.width(32)) shifter_1 (.in(B), .\dist (Shift), .out(shifter_1_out));
  Shifter #(.shift("lr"), .width(32)) shifter_2 (.in(B), .\dist (Shift), .out(shifter_2_out));
  Shifter #(.shift("ar"), .width(32)) shifter_3 (.in(B), .\dist (Shift), .out(shifter_3_out));
  Adder #(.width(32)) adder_1 (.a(A), .b(B), .out(adder_1_out), .cin(CarryIn), .cout(ADC_Cout));
  not not_1 (not_1_out, CarryIn);
  Subtractor #(.width(32)) subtractor_1 (.a(B), .b(A), .out(subtractor_1_out), .bin(not_1_out), .bout(SBC_Cout));
  Shifter #(.shift("rr"), .width(32)) shifter_4 (.in(B), .\dist (Shift), .out(shifter_4_out));
  Negator #(.width(32)) negator_1 (.in(A), .out(negator_1_out));
  Subtractor #(.width(32)) subtractor_2 (.a(B), .b(A), .out(CMP), .bin(1'b0), .bout(CMP_Cout));
  Adder #(.width(32)) adder_2 (.a(A), .b(B), .out(CMN), .cin(1'b0), .cout(CMN_Cout));
  assign or_1_out = B | A;  // OR_Gate or_1, 32 bits wide
  Multiplier #(.width(32)) multiplier_1 (.a(A), .b(B), .out(multiplier_1_out));  // open: cin, cout
  assign and_2_out = B & ~A;  // AND_Gate and_2, 32 bits wide
  assign not_2_out = ~A;  // NOT_Gate not_2, 32 bits wide
  BitSelector #(.width(32)) bitselector_1 (.in(B), .out(bitselector_1_out), .sel({5{1'b1}}));
  BitSelector #(.width(32)) bitselector_2 (.in(A), .out(bitselector_2_out), .sel({5{1'b1}}));
  BitSelector #(.width(32)) bitselector_3 (.in(s_t), .out(bitselector_3_out), .sel({5{1'b1}}));
  Multiplexer #(.select(4), .width(32)) multiplexer_1 (
    .in0(TST), .in1(xor_1_out), .in2(shifter_1_out), .in3(shifter_2_out), .in4(shifter_3_out),
    .in5(adder_1_out), .in6(subtractor_1_out), .in7(shifter_4_out), .in8(TST), .in9(negator_1_out),
    .in10(CMN), .in11(CMP), .in12(or_1_out), .in13(multiplier_1_out), .in14(and_2_out), .in15(not_2_out),
    .out(s_t), .sel(Codop));  // open: en
  // Probe on s_t
  xor xor_2 (xor_2_out, bitselector_1_out, bitselector_2_out);
  xor xor_3 (xor_3_out, bitselector_2_out, bitselector_3_out);
  and and_3 (and_3_out, ~xor_2_out, xor_3_out);  // AND_Gate
  and and_4 (and_4_out, xor_2_out, ~xor_3_out);  // AND_Gate
  // Probe on Flags[2]
  Comparator #(.width(32)) comparator_1 (.a(s_t), .b({32{1'b0}}), .eq(Flags[2]), .lt(Flags[3]));  // open: gt
  // Probe on Flags[3]
  BitSelector #(.width(32)) bitselector_4 (.in(B), .out(bitselector_4_out), .sel(negator_2_out));
  Negator #(.width(5)) negator_2 (.in(Shift), .out(negator_2_out));
  BitSelector #(.width(32)) bitselector_5 (.in(B), .out(bitselector_5_out), .sel(subtractor_3_out));
  Subtractor #(.width(5)) subtractor_3 (.a(Shift), .b(5'b00001), .out(subtractor_3_out));  // open: bin, bout
  Multiplexer #(.select(4)) multiplexer_2 (
    .in0(1'b0), .in1(1'b0), .in2(1'b0), .in3(1'b0), .in4(1'b0), .in5(and_3_out), .in6(and_4_out), .in7(1'b0),
    .in8(1'b0), .in9(1'b0), .in10(and_4_out), .in11(and_3_out), .in12(1'b0), .in13(1'b0), .in14(1'b0),
    .in15(1'b0), .out(Flags[0]), .sel(Codop));  // open: en
  Multiplexer #(.select(4)) multiplexer_3 (
    .in0(1'b0), .in1(1'b0), .in2(bitselector_4_out), .in3(bitselector_5_out), .in4(bitselector_5_out),
    .in5(ADC_Cout), .in6(SBC_Cout), .in7(Flags[3]), .in8(1'b0), .in9(1'b1), .in10(CMP_Cout), .in11(CMN_Cout),
    .in12(1'b0), .in13(1'b0), .in14(1'b0), .in15(1'b0), .out(Flags[1]), .sel(Codop));  // open: en
  Multiplexer #(.enable("false"), .select(4), .width(32)) multiplexer_4 (
    .in0(s_t), .in1(s_t), .in2(s_t), .in3(s_t), .in4(s_t), .in5(s_t), .in6(s_t), .in7(s_t), .in8(B),
    .in9(s_t), .in10(B), .in11(B), .in12(s_t), .in13(s_t), .in14(s_t), .in15(s_t), .out(S), .sel(Codop));

  // Other names for the same wires on the sheet: Cin = CarryIn; V = Flags[0]; C = Flags[1]; Z = Flags[2];
  //   N = Flags[3]

  // Notes on the sheet:
  //   Note: for ROR, C = N
  //   Note 2: assume that shift > 0 for LSL and LSR
endmodule
